// Digital circuit reg_sum_res.dig as structural Verilog
module reg_sum_res (
  input  clk,
  input  Derecha,
  input  clk_2,
  input  Izquierda,
  input  B3,
  input  B2,
  input  B1,
  input  B0,
  input  ADD_SUB,
  input  clk_3,
  output out_3,
  output out_4,
  output out_5,
  output out_6,
  output out_8,
  output out_9,
  output out_10,
  output out_11
);

  wire add_1_s, add_2_c_o, add_2_s, add_3_c_o, add_3_s, add_4_c_o, add_4_s, d_ff_9_q, d_ff_10_q, d_ff_11_q,
       d_ff_12_q, xor_1_out, xor_2_out, xor_3_out, xor_4_out;

  D_FF d_ff_1 (.D(Derecha), .C(clk), .Q(out_6));  // open: nQ
  D_FF d_ff_2 (.D(out_6), .C(clk), .Q(out_5));  // open: nQ
  D_FF d_ff_3 (.D(out_5), .C(clk), .Q(out_4));  // open: nQ
  D_FF d_ff_4 (.D(out_4), .C(clk), .Q(out_3));  // open: nQ
  D_FF d_ff_5 (.D(out_11), .C(clk_2), .Q(out_8));  // open: nQ
  D_FF d_ff_6 (.D(out_10), .C(clk_2), .Q(out_11));  // open: nQ
  D_FF d_ff_7 (.D(out_9), .C(clk_2), .Q(out_10));  // open: nQ
  D_FF d_ff_8 (.D(Izquierda), .C(clk_2), .Q(out_9));  // open: nQ
  xor xor_1 (xor_1_out, B3, ADD_SUB);
  xor xor_2 (xor_2_out, B2, ADD_SUB);
  xor xor_3 (xor_3_out, B1, ADD_SUB);
  xor xor_4 (xor_4_out, B0, ADD_SUB);
  Add add_1 (.a(d_ff_9_q), .b(xor_1_out), .c_i(add_2_c_o), .s(add_1_s));  // open: c_o
  Add add_2 (.a(d_ff_10_q), .b(xor_2_out), .c_i(add_3_c_o), .s(add_2_s), .c_o(add_2_c_o));
  Add add_3 (.a(d_ff_11_q), .b(xor_3_out), .c_i(add_4_c_o), .s(add_3_s), .c_o(add_3_c_o));
  Add add_4 (.a(d_ff_12_q), .b(xor_4_out), .c_i(ADD_SUB), .s(add_4_s), .c_o(add_4_c_o));
  D_FF d_ff_9 (.D(add_1_s), .C(clk_3), .Q(d_ff_9_q));  // open: nQ
  D_FF d_ff_10 (.D(add_2_s), .C(clk_3), .Q(d_ff_10_q));  // open: nQ
  D_FF d_ff_11 (.D(add_3_s), .C(clk_3), .Q(d_ff_11_q));  // open: nQ
  D_FF d_ff_12 (.D(add_4_s), .C(clk_3), .Q(d_ff_12_q));  // open: nQ
  LED led_1 (.in(d_ff_9_q));
  LED led_2 (.in(d_ff_10_q));
  LED led_3 (.in(d_ff_11_q));
  LED led_4 (.in(d_ff_12_q));
endmodule
